// Logisim project Procesador Mips 32 Monociclo.circ as structural Verilog: 8 circuits, main circuit main
module main (
  input  Reset
);

  wire alu_1_zero, alucontrol_1_jr, and_2_out, CLK, clock_1_out, comparator_1_eq, comparator_2_eq,
       comparator_3_eq, control_1_alusrc, control_1_branch, control_1_memread, control_1_memtoreg,
       control_1_memwrite, control_1_regdst, control_1_regwrite, JAL, not_1_out, not_2_out, or_1_out;
  wire [1:0] control_1_aluop;
  wire [2:0] alucontrol_1_operation;
  wire [4:0] breakdown_1_rd, breakdown_1_rs, breakdown_1_rt, multiplexer_1_out, multiplexer_2_out;
  wire [5:0] breakdown_1_funct, breakdown_1_opcode;
  wire [15:0] breakdown_1_inmediate;
  wire [25:0] breakdown_1_address, shifter_1_out;
  wire [27:0] bit_extender_3_out;
  wire [31:0] adder_1_out, alu_1_result, bit_extender_1_out, bit_extender_2_out, datamemory_1_readdata,
       ifetch_1_instruction, ifetch_1_pc_4, multiplexer_3_out, multiplexer_4_out, multiplexer_5_out,
       multiplexer_6_out, multiplexer_7_out, multiplexer_8_out, multiplexer_9_out, regfile_1_readdata1,
       regfile_1_readdata2, shifter_2_out;

  // Probe on ifetch_1_instruction
  // Probe on multiplexer_7_out
  // Probe on multiplexer_7_out
  Comparator #(.width(32)) comparator_1 (
    .a(ifetch_1_instruction), .b({32{1'b0}}), .eq(comparator_1_eq));  // open: gt, lt
  // Probe on ifetch_1_pc_4
  IFetch ifetch_1 (
    .PC_Next(multiplexer_7_out), .CLK(CLK), .Reset(Reset), .PC_4(ifetch_1_pc_4),
    .Instruction(ifetch_1_instruction));
  Clock #(.phaseOffset(2)) clock_1 (.out(clock_1_out));
  not not_1 (not_1_out, comparator_1_eq);
  and and_1 (CLK, clock_1_out, not_1_out);
  BreakDown breakdown_1 (
    .Instruction(ifetch_1_instruction), .Funct(breakdown_1_funct), .RD(breakdown_1_rd), .RT(breakdown_1_rt),
    .RS(breakdown_1_rs), .OpCode(breakdown_1_opcode), .Inmediate(breakdown_1_inmediate),
    .Address(breakdown_1_address));  // open: Shamt
  Shifter #(.width(26)) shifter_1 (.in(breakdown_1_address), .\dist (5'b00010), .out(shifter_1_out));
  Multiplexer #(.width(5)) multiplexer_1 (
    .in0(breakdown_1_rt), .in1(breakdown_1_rd), .out(multiplexer_1_out), .sel(control_1_regdst));
  Multiplexer #(.width(5)) multiplexer_2 (.in0(multiplexer_1_out), .in1({5{1'b1}}), .out(multiplexer_2_out), .sel(JAL));
  assign bit_extender_1_out = {{16{1'b0}}, breakdown_1_inmediate};  // Bit_Extender bit_extender_1
  assign bit_extender_2_out = {{16{breakdown_1_inmediate[15]}}, breakdown_1_inmediate};  // Bit_Extender bit_extender_2
  Comparator #(.width(6)) comparator_2 (.a(6'b001100), .b(breakdown_1_opcode), .eq(comparator_2_eq));  // open: gt, lt
  Comparator #(.width(6)) comparator_3 (.a(6'b100101), .b(breakdown_1_opcode), .eq(comparator_3_eq));  // open: gt, lt
  // Probe on {ifetch_1_pc_4[31:28], bit_extender_3_out}
  Multiplexer #(.width(32)) multiplexer_3 (
    .in0(bit_extender_1_out), .in1(bit_extender_2_out), .out(multiplexer_3_out), .sel(not_2_out));
  not not_2 (not_2_out, or_1_out);
  or or_1 (or_1_out, comparator_2_eq, comparator_3_eq);
  assign bit_extender_3_out = {{2{shifter_1_out[25]}}, shifter_1_out};  // Bit_Extender bit_extender_3
  Control control_1 (
    .Opcode(breakdown_1_opcode), .RegDst(control_1_regdst), .Jump(JAL), .Branch(control_1_branch),
    .MemRead(control_1_memread), .MemtoReg(control_1_memtoreg), .ALUOp(control_1_aluop),
    .MemWrite(control_1_memwrite), .ALUSrc(control_1_alusrc), .RegWrite(control_1_regwrite));
  RegFile regfile_1 (
    .ReadReg1(breakdown_1_rs), .ReadReg2(breakdown_1_rt), .RegWrite(control_1_regwrite),
    .WriteReg(multiplexer_2_out), .WriteData(multiplexer_9_out), .CLK(CLK), .Reset(Reset),
    .ReadData1(regfile_1_readdata1), .ReadData2(regfile_1_readdata2));
  Multiplexer #(.width(32)) multiplexer_4 (
    .in0(regfile_1_readdata2), .in1(multiplexer_3_out), .out(multiplexer_4_out), .sel(control_1_alusrc));
  Shifter #(.width(32)) shifter_2 (.in(multiplexer_3_out), .\dist (5'b00010), .out(shifter_2_out));
  ALUControl alucontrol_1 (
    .ALUOp(control_1_aluop), .Funct(breakdown_1_funct), .Jr(alucontrol_1_jr),
    .Operation(alucontrol_1_operation));
  Adder #(.width(32)) adder_1 (.a(ifetch_1_pc_4), .b(shifter_2_out), .out(adder_1_out));  // open: cin, cout
  ALU alu_1 (
    .In1(regfile_1_readdata1), .In2(multiplexer_4_out), .ALUOperation(alucontrol_1_operation),
    .Zero(alu_1_zero), .Result(alu_1_result));
  Multiplexer #(.width(32)) multiplexer_5 (
    .in0(ifetch_1_pc_4), .in1(adder_1_out), .out(multiplexer_5_out), .sel(and_2_out));
  and and_2 (and_2_out, control_1_branch, alu_1_zero);
  Multiplexer #(.width(32)) multiplexer_6 (
    .in0(multiplexer_5_out), .in1({ifetch_1_pc_4[31:28], bit_extender_3_out}), .out(multiplexer_6_out),
    .sel(JAL));
  Multiplexer #(.width(32)) multiplexer_7 (
    .in0(multiplexer_6_out), .in1(regfile_1_readdata1), .out(multiplexer_7_out), .sel(alucontrol_1_jr));
  DataMemory datamemory_1 (
    .Address(alu_1_result), .WriteData(regfile_1_readdata2), .MemWrite(control_1_memwrite),
    .MemRead(control_1_memread), .CLK(CLK), .Reset(Reset), .ReadData(datamemory_1_readdata));
  Multiplexer #(.width(32)) multiplexer_8 (
    .in0(alu_1_result), .in1(datamemory_1_readdata), .out(multiplexer_8_out), .sel(control_1_memtoreg));
  Multiplexer #(.width(32)) multiplexer_9 (
    .in0(multiplexer_8_out), .in1(ifetch_1_pc_4), .out(multiplexer_9_out), .sel(JAL));
endmodule

module RegFile (
  input  [4:0] ReadReg1,
  input  [4:0] ReadReg2,
  input  RegWrite,
  input  [4:0] WriteReg,
  input  [31:0] WriteData,
  input  CLK,
  input  Reset,
  output [31:0] ReadData1,
  output [31:0] ReadData2
);

  wire and_1_out, comparator_1_lt, comparator_2_gt, or_1_out, WE0, WE1, WE2, WE3, WE4, WE5, WE6, WE7, WE8,
       WE9, WE10, WE11, WE12, WE13, WE14, WE15, WE16, WE17, WE18, WE19, WE20, WE21, WE22, WE23, WE24, WE25,
       WE26, WE27, WE28, WE29, WE30, WE31;
  wire [31:0] R0, R1, R2, R3, R4, R5, R6, R7, R8, R9, R10, R11, R12, R13, R14, R15, R16, R17, R18, R19, R20,
       R21, R22, R23, R24, R25, R26, R27, R28, R29, R30, R31;

  Decoder #(.select(5)) decoder_1 (
    .out0(WE0), .out1(WE1), .out2(WE2), .out3(WE3), .out4(WE4), .out5(WE5), .out6(WE6), .out7(WE7),
    .out8(WE8), .out9(WE9), .out10(WE10), .out11(WE11), .out12(WE12), .out13(WE13), .out14(WE14),
    .out15(WE15), .out16(WE16), .out17(WE17), .out18(WE18), .out19(WE19), .out20(WE20), .out21(WE21),
    .out22(WE22), .out23(WE23), .out24(WE24), .out25(WE25), .out26(WE26), .out27(WE27), .out28(WE28),
    .out29(WE29), .out30(WE30), .out31(WE31), .sel(WriteReg), .en(RegWrite));
  Register #(.width(32)) zero (.D(WriteData), .en(1'b0), .Q(R0), .clk(and_1_out), .clr(Reset));
  Register #(.width(32)) at (.D(WriteData), .en(WE1), .Q(R1), .clk(and_1_out), .clr(Reset));
  Register #(.width(32)) v0 (.D(WriteData), .en(WE2), .Q(R2), .clk(and_1_out), .clr(Reset));
  Register #(.width(32)) v1 (.D(WriteData), .en(WE3), .Q(R3), .clk(and_1_out), .clr(Reset));
  Register #(.width(32)) a0 (.D(WriteData), .en(WE4), .Q(R4), .clk(and_1_out), .clr(Reset));
  Register #(.width(32)) a1 (.D(WriteData), .en(WE5), .Q(R5), .clk(and_1_out), .clr(Reset));
  Register #(.width(32)) a2 (.D(WriteData), .en(WE6), .Q(R6), .clk(and_1_out), .clr(Reset));
  Register #(.width(32)) a3 (.D(WriteData), .en(WE7), .Q(R7), .clk(and_1_out), .clr(Reset));
  Comparator #(.width(32)) comparator_1 (.a(WriteData), .b(32'h7fffffff), .lt(comparator_1_lt));  // open: gt, eq
  Comparator #(.width(32)) comparator_2 (.a(WriteData), .b(32'h80000000), .gt(comparator_2_gt));  // open: eq, lt
  Multiplexer #(.select(5), .width(32)) multiplexer_1 (
    .in0(R0), .in1(R1), .in2(R2), .in3(R3), .in4(R4), .in5(R5), .in6(R6), .in7(R7), .in8(R8), .in9(R9),
    .in10(R10), .in11(R11), .in12(R12), .in13(R13), .in14(R14), .in15(R15), .in16(R16), .in17(R17),
    .in18(R18), .in19(R19), .in20(R20), .in21(R21), .in22(R22), .in23(R23), .in24(R24), .in25(R25),
    .in26(R26), .in27(R27), .in28(R28), .in29(R29), .in30(R30), .in31(R31), .out(ReadData1), .sel(ReadReg1));
  or or_1 (or_1_out, comparator_1_lt, comparator_2_gt);
  Register #(.width(32)) t0 (.D(WriteData), .en(WE8), .Q(R8), .clk(and_1_out), .clr(Reset));
  Register #(.width(32)) t1 (.D(WriteData), .en(WE9), .Q(R9), .clk(and_1_out), .clr(Reset));
  Register #(.width(32)) t2 (.D(WriteData), .en(WE10), .Q(R10), .clk(and_1_out), .clr(Reset));
  Register #(.width(32)) t3 (.D(WriteData), .en(WE11), .Q(R11), .clk(and_1_out), .clr(Reset));
  and and_1 (and_1_out, CLK, or_1_out);
  Register #(.width(32)) t4 (.D(WriteData), .en(WE12), .Q(R12), .clk(and_1_out), .clr(Reset));
  Register #(.width(32)) t5 (.D(WriteData), .en(WE13), .Q(R13), .clk(and_1_out), .clr(Reset));
  Register #(.width(32)) t6 (.D(WriteData), .en(WE14), .Q(R14), .clk(and_1_out), .clr(Reset));
  Register #(.width(32)) t7 (.D(WriteData), .en(WE15), .Q(R15), .clk(and_1_out), .clr(Reset));
  Multiplexer #(.select(5), .width(32)) multiplexer_2 (
    .in0(R0), .in1(R1), .in2(R2), .in3(R3), .in4(R4), .in5(R5), .in6(R6), .in7(R7), .in8(R8), .in9(R9),
    .in10(R10), .in11(R11), .in12(R12), .in13(R13), .in14(R14), .in15(R15), .in16(R16), .in17(R17),
    .in18(R18), .in19(R19), .in20(R20), .in21(R21), .in22(R22), .in23(R23), .in24(R24), .in25(R25),
    .in26(R26), .in27(R27), .in28(R28), .in29(R29), .in30(R30), .in31(R31), .out(ReadData2), .sel(ReadReg2));
  Register #(.width(32)) s0 (.D(WriteData), .en(WE16), .Q(R16), .clk(and_1_out), .clr(Reset));
  Register #(.width(32)) s1 (.D(WriteData), .en(WE17), .Q(R17), .clk(and_1_out), .clr(Reset));
  Register #(.width(32)) s2 (.D(WriteData), .en(WE18), .Q(R18), .clk(and_1_out), .clr(Reset));
  Register #(.width(32)) s3 (.D(WriteData), .en(WE19), .Q(R19), .clk(and_1_out), .clr(Reset));
  Register #(.width(32)) s4 (.D(WriteData), .en(WE20), .Q(R20), .clk(and_1_out), .clr(Reset));
  Register #(.width(32)) s5 (.D(WriteData), .en(WE21), .Q(R21), .clk(and_1_out), .clr(Reset));
  Register #(.width(32)) s6 (.D(WriteData), .en(WE22), .Q(R22), .clk(and_1_out), .clr(Reset));
  Register #(.width(32)) s7 (.D(WriteData), .en(WE23), .Q(R23), .clk(and_1_out), .clr(Reset));
  Register #(.width(32)) t8 (.D(WriteData), .en(WE24), .Q(R24), .clk(and_1_out), .clr(Reset));
  Register #(.width(32)) t9 (.D(WriteData), .en(WE25), .Q(R25), .clk(and_1_out), .clr(Reset));
  Register #(.width(32)) k0 (.D(WriteData), .en(WE26), .Q(R26), .clk(and_1_out), .clr(Reset));
  Register #(.width(32)) k1 (.D(WriteData), .en(WE27), .Q(R27), .clk(and_1_out), .clr(Reset));
  Register #(.width(32)) gp (.D(WriteData), .en(WE28), .Q(R28), .clk(and_1_out), .clr(Reset));
  Register #(.width(32)) sp (.D(WriteData), .en(WE29), .Q(R29), .clk(and_1_out), .clr(Reset));
  Register #(.width(32)) fp (.D(WriteData), .en(WE30), .Q(R30), .clk(and_1_out), .clr(Reset));
  Register #(.width(32)) ra (.D(WriteData), .en(WE31), .Q(R31), .clk(and_1_out), .clr(Reset));
endmodule

module ALU (
  input  [31:0] In1,
  input  [31:0] In2,
  input  [2:0] ALUOperation,
  output Zero,
  output [31:0] Result
);

  wire [0:0] comparator_1_lt;
  wire [31:0] adder_1_out, and_1_out, nor_1_out, or_1_out, subtractor_1_out;

  Subtractor #(.width(32)) subtractor_1 (.a(In1), .b(In2), .out(subtractor_1_out));  // open: bin, bout
  Adder #(.width(32)) adder_1 (.a(In1), .b(In2), .out(adder_1_out));  // open: cin, cout
  Comparator #(.width(32)) comparator_1 (.a(In1), .b(In2), .lt(comparator_1_lt[0]));  // open: gt, eq
  assign and_1_out = In1 & In2;  // AND_Gate and_1, 32 bits wide
  assign nor_1_out = ~(In1 | In2);  // NOR_Gate nor_1, 32 bits wide
  assign or_1_out = In1 | In2;  // OR_Gate or_1, 32 bits wide
  Multiplexer #(.select(3), .width(32)) multiplexer_1 (
    .in0(subtractor_1_out), .in1(adder_1_out), .in2({{31{1'b0}}, comparator_1_lt[0]}), .in4(and_1_out),
    .in5(nor_1_out), .in6(or_1_out), .out(Result), .sel(ALUOperation));  // open: in3, in7
  Comparator #(.width(32)) comparator_2 (.a(Result), .b({32{1'b0}}), .eq(Zero));  // open: gt, lt

  // Notes on the sheet:
  //   SUB = 000
  //   ADD = 001
  //   SLT = 010
  //   AND = 100
  //   NOR = 101
  //   OR = 110
  //   SUB
  //   ADD
  //   SLT
  //   AND
  //   NOR
  //   OR
endmodule

module BreakDown (
  input  [31:0] Instruction,
  output [5:0] Funct,
  output [4:0] Shamt,
  output [4:0] RD,
  output [4:0] RT,
  output [4:0] RS,
  output [5:0] OpCode,
  output [15:0] Inmediate,
  output [25:0] Address
);


  assign Address = Instruction[25:0];
  assign Funct = Instruction[5:0];
  assign Inmediate = Instruction[15:0];
  assign OpCode = Instruction[31:26];
  assign RD = Instruction[15:11];
  assign RS = Instruction[25:21];
  assign RT = Instruction[20:16];
  assign Shamt = Instruction[10:6];
endmodule

module IFetch (
  input  [31:0] PC_Next,
  input  CLK,
  input  Reset,
  output [31:0] PC_4,
  output [31:0] Instruction
);

  wire [31:0] register_1_q;

  Register #(.width(32)) register_1 (.D(PC_Next), .en(1'b1), .Q(register_1_q), .clk(CLK), .clr(Reset));
  // Probe on register_1_q
  Adder #(.width(32)) adder_1 (.a(register_1_q), .b(32'h4), .out(PC_4));  // open: cin, cout
  ROM #(.addrWidth(24), .dataWidth(32)) rom_1 (.addr(register_1_q[25:2]), .data(Instruction));
  // Probe on register_1_q
  // Probe on register_1_q

  // Notes on the sheet:
  //   contents of rom_1 (hex, n*v repeats v):
  //   94040040 8c050000 8c06004c 8c070050 8c100054 8c110060 8c120040 8c130064 8c140068 8c15005c 8c160058
  //   4020 4820 5020 8c050000 2820 d2582a 3820 2820 11730001 800002a f4582a 11730002 d33020 8000010
  //   8cae0000 8caf0004 1cf582a 11730004 f33820 1956820 b52820 8000015 8cb60000 8cac0004 2c06825 acac0000
  //   acae0004 f33820 1956820 b52820 8000015 8c100044 8c110048 2820 5020 1144000c 8ca80000 31090001
  //   11200001 8000037 2138020 b52820 1535020 800002e 2338820 b52820 1535020 800002e ac100044 ac110048
  //   c00003f 8000052 8bc827 295c022 8c040000 8c050004 8c060008 8c07000c 8c080010 8c090014 8c0a0018
  //   8c0b001c 8c0c0020 8c0d0024 8c0e0028 8c0f002c 8c120030 8c130034 8c140038 8c15003c 3e00008
  //   PC
endmodule

module DataMemory (
  input  [31:0] Address,
  input  [31:0] WriteData,
  input  MemWrite,
  input  MemRead,
  input  CLK,
  input  Reset,
  output [31:0] ReadData
);

  RAM #(.addrWidth(24), .asyncread("true"), .clearpin("true"), .dataWidth(32), .trigger("falling")) ram_1 (
    .addr(Address[25:2]), .we(MemWrite), .oe(MemRead), .clk(CLK), .din(WriteData), .dout(ReadData),
    .clr(Reset));
endmodule

module ALUControl (
  input  [1:0] ALUOp,
  input  [5:0] Funct,
  output Jr,
  output [2:0] Operation
);

  wire and_2_out, and_3_out, and_4_out, and_5_out, and_6_out, and_7_out, and_8_out, not_1_out, not_2_out,
       not_3_out, not_4_out, not_5_out, not_6_out, not_7_out;

  not not_1 (not_1_out, ALUOp[1]);
  not not_2 (not_2_out, ALUOp[0]);
  not not_3 (not_3_out, Funct[5]);
  not not_4 (not_4_out, Funct[4]);
  not not_5 (not_5_out, Funct[2]);
  not not_6 (not_6_out, Funct[1]);
  not not_7 (not_7_out, Funct[0]);
  and and_1 (Jr, ALUOp[1], not_2_out, not_3_out, not_4_out, Funct[3], not_5_out, not_6_out, not_7_out);
  and and_2 (and_2_out, ALUOp[1], Funct[2]);
  and and_3 (and_3_out, ALUOp[1], ALUOp[0]);
  and and_4 (and_4_out, ALUOp[1], not_2_out, not_6_out, Funct[0]);
  and and_5 (and_5_out, ALUOp[1], not_2_out, Funct[3]);
  and and_6 (and_6_out, not_2_out, not_5_out, not_6_out);
  and and_7 (and_7_out, not_1_out, not_2_out);
  and and_8 (and_8_out, not_2_out, Funct[1], Funct[0]);
  or or_1 (Operation[2], and_2_out, and_3_out);
  or or_2 (Operation[1], and_4_out, and_5_out);
  or or_3 (Operation[0], and_6_out, and_7_out, and_8_out);
endmodule

module Control (
  input  [5:0] Opcode,
  output RegDst,
  output Jump,
  output Branch,
  output MemRead,
  output MemtoReg,
  output [1:0] ALUOp,
  output MemWrite,
  output ALUSrc,
  output RegWrite
);

  wire and_5_out, and_6_out, and_7_out, and_8_out, and_9_out, and_10_out, and_11_out, and_12_out, and_13_out,
       and_14_out, and_16_out, and_17_out, and_18_out, and_19_out, and_20_out, and_21_out, and_22_out,
       not_1_out, not_2_out, not_3_out, not_4_out, not_5_out, not_6_out;

  not not_1 (not_1_out, Opcode[5]);
  not not_2 (not_2_out, Opcode[4]);
  not not_3 (not_3_out, Opcode[3]);
  not not_4 (not_4_out, Opcode[2]);
  not not_5 (not_5_out, Opcode[1]);
  not not_6 (not_6_out, Opcode[0]);
  and and_1 (RegDst, not_3_out, not_6_out);
  and and_2 (Jump, not_1_out, not_2_out, not_3_out, not_4_out, Opcode[1]);
  and and_3 (Branch, not_3_out, Opcode[2], not_6_out);
  and and_4 (MemRead, Opcode[5], not_3_out);
  and and_5 (and_5_out, not_3_out, Opcode[0]);
  and and_6 (and_6_out, not_1_out, Opcode[1], Opcode[0]);
  and and_7 (and_7_out, Opcode[2], Opcode[0]);
  and and_8 (and_8_out, Opcode[4], Opcode[0]);
  and and_9 (and_9_out, Opcode[5], not_5_out, Opcode[0]);
  and and_10 (and_10_out, not_3_out, not_4_out, not_5_out);
  and and_11 (and_11_out, Opcode[3], Opcode[2], not_5_out);
  and and_12 (and_12_out, not_4_out, not_5_out, not_6_out);
  and and_13 (and_13_out, Opcode[5], not_4_out, not_5_out);
  and and_14 (and_14_out, Opcode[4], not_4_out, not_5_out);
  and and_15 (ALUOp[0], Opcode[2], not_6_out);
  and and_16 (and_16_out, Opcode[5], not_3_out, not_4_out, not_5_out);
  and and_17 (and_17_out, Opcode[5], not_3_out, not_4_out, not_6_out);
  and and_18 (and_18_out, Opcode[5], Opcode[4], not_3_out, not_4_out);
  and and_19 (and_19_out, Opcode[5], not_2_out, Opcode[3], not_4_out, Opcode[1], Opcode[0]);
  or or_1 (ALUSrc, Opcode[0], Opcode[3]);
  and and_20 (and_20_out, not_4_out, not_5_out);
  and and_21 (and_21_out, not_3_out, Opcode[0]);
  and and_22 (and_22_out, Opcode[3], not_5_out);
  or or_2 (MemtoReg, and_5_out, and_6_out, and_7_out, and_8_out, and_9_out);
  or or_3 (ALUOp[1], and_10_out, and_11_out, and_12_out, and_13_out, and_14_out);
  or or_4 (MemWrite, and_16_out, and_17_out, and_18_out, and_19_out);
  or or_5 (RegWrite, and_20_out, and_21_out, and_22_out);
endmodule
